// Logisim project processor-surprise.circ as structural Verilog
module ALU (
  input  [2:0] F,
  input  [31:0] in_2,
  input  [31:0] B,
  input  [31:0] A,
  output zero,
  output [31:0] Y
);

  wire [30:0] adder_1_out;
  wire [31:0] and_1_out, bit_extender_1_out, multiplexer_1_out, multiplexer_3_out, multiplier_1_out,
       not_1_out, or_1_out;
  wire [31:31] adder_1_out_2;

  assign not_1_out = ~B;  // NOT_Gate not_1, 32 bits wide
  Multiplexer #(.width(32)) multiplexer_1 (.in0(B), .in1(not_1_out), .out(multiplexer_1_out));  // open: sel
  Adder #(.width(32)) adder_1 (
    .a(multiplexer_1_out), .b(A), .out({adder_1_out_2[31], adder_1_out}), .cin(F[2]));  // open: cout
  assign and_1_out = multiplexer_1_out & A;  // AND_Gate and_1, 32 bits wide
  assign or_1_out = multiplexer_1_out | A;  // OR_Gate or_1, 32 bits wide
  assign bit_extender_1_out = {{31{1'b0}}, adder_1_out_2[31]};  // Bit_Extender bit_extender_1
  Multiplier #(.width(32)) multiplier_1 (.a(A), .b(B), .out(multiplier_1_out));  // open: cin, cout
  Multiplexer #(.select(2), .width(32)) multiplexer_2 (
    .in0(and_1_out), .in1(or_1_out), .in2({adder_1_out_2[31], adder_1_out}), .in3(multiplexer_3_out), .out(Y));  // open: sel
  Multiplexer #(.width(32)) multiplexer_3 (
    .in0(multiplier_1_out), .in1(bit_extender_1_out), .out(multiplexer_3_out), .sel(F[2]));
  Comparator #(.width(32)) comparator_1 (.a(Y), .b(in_2), .eq(zero));  // open: gt, lt
endmodule

module Datapath (
  input  Restart,
  output [31:0] v0
);

  wire alu_1_zero, and_1_out, clock_1_out, controlunit_1_alusrc, controlunit_1_branch, controlunit_1_regdst,
       controlunit_1_regwrite;
  wire [2:0] bitselector_1_out, bitselector_2_out, bitselector_4_out, controlunit_1_alucontrol,
       multiplexer_3_out;
  wire [7:0] adder_1_out, adder_2_out, bitselector_5_out, multiplexer_1_out, multiplexer_2_out, register_1_q,
       shifter_1_out, shifter_4_out;
  wire [15:0] bitselector_3_out;
  wire [31:0] alu_1_y, bit_extender_1_out, multiplexer_4_out, registerfile_1_rd1, registerfile_1_rd2,
       rom_1_data, shifter_2_out, shifter_3_out;

  Multiplexer #(.width(8)) multiplexer_1 (.in0(adder_1_out), .in1(adder_2_out), .out(multiplexer_1_out));  // open: sel
  Clock clock_1 (.out(clock_1_out));
  Multiplexer #(.width(8)) multiplexer_2 (
    .in0(multiplexer_1_out), .in1({8{1'b0}}), .out(multiplexer_2_out), .sel(Restart));
  Register register_1 (.D(multiplexer_2_out), .Q(register_1_q), .clk(clock_1_out));  // open: en, clr
  Adder adder_1 (.a(8'h4), .b(register_1_q), .out(adder_1_out));  // open: cin, cout
  Shifter #(.shift("lr")) shifter_1 (.in(register_1_q), .\dist (3'b010), .out(shifter_1_out));
  ROM #(.dataWidth(32)) rom_1 (.addr(shifter_1_out), .data(rom_1_data));
  Shifter #(.shift("lr"), .width(32)) shifter_2 (.in(rom_1_data), .\dist (5'b10000), .out(shifter_2_out));
  BitSelector #(.group(3), .width(32)) bitselector_1 (.in(rom_1_data), .out(bitselector_1_out), .sel(4'b0111));
  BitSelector #(.group(3), .width(32)) bitselector_2 (.in(shifter_2_out), .out(bitselector_2_out), .sel(4'b0000));
  Shifter #(.shift("lr"), .width(32)) shifter_3 (.in(rom_1_data), .\dist (5'b01011), .out(shifter_3_out));
  BitSelector #(.group(16), .width(32)) bitselector_3 (.in(rom_1_data), .out(bitselector_3_out), .sel(1'b0));
  ControlUnit controlunit_1 (
    .Instruction(rom_1_data), .RegWrite(controlunit_1_regwrite), .ALUSrc(controlunit_1_alusrc),
    .ALUControl(controlunit_1_alucontrol), .Branch(controlunit_1_branch), .RegDst(controlunit_1_regdst));
  RegisterFile registerfile_1 (
    .CLK(clock_1_out), .A1(bitselector_1_out), .WD3(alu_1_y), .A2(bitselector_2_out),
    .WE3(controlunit_1_regwrite), .A3(multiplexer_3_out), .RD1(registerfile_1_rd1), .RD2(registerfile_1_rd2),
    .V0(v0));
  Multiplexer #(.width(3)) multiplexer_3 (
    .in0(bitselector_2_out), .in1(bitselector_4_out), .out(multiplexer_3_out));  // open: sel
  BitSelector #(.group(3), .width(32)) bitselector_4 (.in(shifter_3_out), .out(bitselector_4_out), .sel(4'b0000));
  assign bit_extender_1_out = {{16{bitselector_3_out[15]}}, bitselector_3_out};  // Bit_Extender bit_extender_1
  BitSelector #(.group(8), .width(16)) bitselector_5 (.in(bitselector_3_out), .out(bitselector_5_out), .sel(1'b0));
  Multiplexer #(.width(32)) multiplexer_4 (
    .in0(registerfile_1_rd2), .in1(bit_extender_1_out), .out(multiplexer_4_out));  // open: sel
  Shifter shifter_4 (.in(bitselector_5_out), .\dist (3'b010), .out(shifter_4_out));
  Adder adder_2 (.a(shifter_4_out), .b(adder_1_out), .out(adder_2_out));  // open: cin, cout
  ALU alu_1 (
    .F(controlunit_1_alucontrol), .B(registerfile_1_rd1), .A(multiplexer_4_out), .zero(alu_1_zero),
    .Y(alu_1_y));  // open: in_2
  and and_1 (and_1_out, controlunit_1_branch, alu_1_zero);

  // Notes on the sheet:
  //   CLK
  //   Write A1-A3 as 5 bit, but program only mask 3 of 5 
  //   contents of rom_1 (hex, n*v repeats v):
  //   20040009 20020001 20050001 10850004 70441002 2084ffff 1000fffc 20 1000ffff 20
  //   A1 / 25:21
  //   A2 / 20:16
  //   A2 / 20:16
  //   A3 / 15:11
  //   imm / 15:0
  //   Hex
endmodule

module Tests (
  output [15:0] out_1,
  output [25:0] out_2,
  output [31:0] Y,
  output [2:0] out_4,
  output [2:0] out_5,
  output [2:0] out_6,
  output [2:0] out_7,
  output [7:0] out_8,
  output [2:0] out_9
);

  wire [31:0] shifter_1_out, shifter_2_out;

  BitSelector #(.group(3), .width(32)) bitselector_1 (.in(32'h12356789), .out(out_6), .sel(4'b0111));
  BitSelector #(.group(8), .width(32)) bitselector_2 (.in(32'h12356789), .out(out_8), .sel(2'b01));
  BitSelector #(.group(3)) bitselector_3 (.in(out_8), .out(out_9), .sel(2'b00));
  BitSelector #(.group(16), .width(32)) bitselector_4 (.in(32'h20411809), .out(out_1), .sel(1'b0));
  Shifter #(.shift("lr"), .width(32)) shifter_1 (.in(32'h20411809), .\dist (5'b01011), .out(shifter_1_out));
  Shifter #(.shift("lr"), .width(32)) shifter_2 (.in(32'h20411809), .\dist (5'b10000), .out(shifter_2_out));
  BitSelector #(.group(3), .width(32)) bitselector_5 (.in(32'h20411809), .out(out_7), .sel(4'b0111));
  BitSelector #(.group(3), .width(32)) bitselector_6 (.in(shifter_1_out), .out(out_4), .sel(4'b0000));
  BitSelector #(.group(3), .width(32)) bitselector_7 (.in(shifter_2_out), .out(out_5), .sel(4'b0000));
  BitSelector #(.group(26), .width(32)) bitselector_8 (.in(32'h20411809), .out(out_2), .sel(1'b0));

  assign Y = 32'hf4010207;

  // Notes on the sheet:
  //   binary values in Logisim. Convince yourself how the bits are displayed.
  //   Example 2: The bit selector is configured to have 32  
  //   bit group #1 (starting at index 0) is selected for the output.
  //   That is, the 8 bits 0x67 at bit indices 15..8  are sent to the output.
  //   Example 3: Now, assume that you want to extract 3 bits at   
  //   Example 1: A simple example that illustrates how 32-bit values are displayed as 
  //   input bits and 8 output bits. The parameter constant is 1, which means that   
  //   bit indices 10..8. This can be accoplished by putting two bit selecotrs in series.
  //   15:0
  //   A3 / 15:11
  //   A2 / 20:16
  //   A1 / 25:21
  //   25:0
endmodule

module RegisterFile (
  input  CLK,
  input  [2:0] A1,
  input  [31:0] WD3,
  input  [2:0] A2,
  input  WE3,
  input  [2:0] A3,
  output [31:0] RD1,
  output [31:0] RD2,
  output [31:0] V0
);

  wire and_1_out, and_2_out, and_3_out, and_4_out, and_5_out, and_6_out, and_7_out, and_8_out,
       decoder_1_out0, decoder_1_out1, decoder_1_out2, decoder_1_out3, decoder_1_out4, decoder_1_out5,
       decoder_1_out6, decoder_1_out7;
  wire [31:0] register_1_q, register_3_q, register_4_q, register_5_q, register_6_q, register_7_q,
       register_8_q;

  Decoder #(.select(3)) decoder_1 (
    .out0(decoder_1_out0), .out1(decoder_1_out1), .out2(decoder_1_out2), .out3(decoder_1_out3),
    .out4(decoder_1_out4), .out5(decoder_1_out5), .out6(decoder_1_out6), .out7(decoder_1_out7), .sel(A3));  // open: en
  and and_1 (and_1_out, WE3, decoder_1_out1);
  and and_2 (and_2_out, WE3, decoder_1_out2);
  and and_3 (and_3_out, WE3, decoder_1_out3);
  and and_4 (and_4_out, WE3, decoder_1_out4);
  and and_5 (and_5_out, WE3, decoder_1_out5);
  and and_6 (and_6_out, WE3, decoder_1_out6);
  and and_7 (and_7_out, WE3, decoder_1_out7);
  and and_8 (and_8_out, decoder_1_out0, decoder_1_out7);
  Register #(.width(32)) register_1 (.D(WD3), .en(and_1_out), .Q(register_1_q), .clk(CLK));  // open: clr
  Register #(.width(32)) register_2 (.D(WD3), .en(and_2_out), .Q(V0), .clk(CLK));  // open: clr
  Register #(.width(32)) register_3 (.D(WD3), .en(and_3_out), .Q(register_3_q), .clk(CLK));  // open: clr
  Register #(.width(32)) register_4 (.D(WD3), .en(and_4_out), .Q(register_4_q), .clk(CLK));  // open: clr
  Register #(.width(32)) register_5 (.D(WD3), .en(and_5_out), .Q(register_5_q), .clk(CLK));  // open: clr
  Register #(.width(32)) register_6 (.D(WD3), .en(and_6_out), .Q(register_6_q), .clk(CLK));  // open: clr
  Register #(.width(32)) register_7 (.D(WD3), .en(and_7_out), .Q(register_7_q), .clk(CLK));  // open: clr
  Register #(.width(32)) register_8 (.D({32{1'b0}}), .en(and_8_out), .Q(register_8_q), .clk(CLK));  // open: clr
  Multiplexer #(.enable("true"), .select(3), .width(32)) multiplexer_1 (
    .in0(register_8_q), .in1(register_1_q), .in2(V0), .in3(register_3_q), .in4(register_4_q),
    .in5(register_5_q), .in6(register_6_q), .in7(register_7_q), .out(RD1), .sel(A1));  // open: en
  Multiplexer #(.enable("true"), .select(3), .width(32)) multiplexer_2 (
    .in0(register_8_q), .in1(register_1_q), .in2(V0), .in3(register_3_q), .in4(register_4_q),
    .in5(register_5_q), .in6(register_6_q), .in7(register_7_q), .out(RD2), .sel(A2));  // open: en

  // Notes on the sheet:
  //   and_8 drives only 1 and floats otherwise
endmodule

module ControlUnit (
  input  [31:0] Instruction,
  output RegDst,
  output RegWrite,
  output ALUSrc,
  output [2:0] ALUControl,
  output Branch
);

  wire comparator_2_eq, comparator_4_eq;
  wire [2:0] multiplexer_1_out;
  wire [5:0] bitselector_1_out;
  wire [31:0] shifter_1_out;

  Shifter #(.shift("lr"), .width(32)) shifter_1 (.in(Instruction), .\dist (5'b11010), .out(shifter_1_out));
  BitSelector #(.group(6), .width(32)) bitselector_1 (.in(shifter_1_out), .out(bitselector_1_out), .sel(3'b000));
  Comparator #(.mode("unsigned"), .width(6)) comparator_1 (
    .a(bitselector_1_out), .b(6'b001000), .eq(ALUSrc));  // open: gt, lt
  Comparator #(.mode("unsigned"), .width(6)) comparator_2 (
    .a(bitselector_1_out), .b({6{1'b0}}), .eq(comparator_2_eq));  // open: gt, lt
  Comparator #(.mode("unsigned"), .width(6)) comparator_3 (
    .a(bitselector_1_out), .b(6'b000100), .eq(Branch));  // open: gt, lt
  Comparator #(.mode("unsigned"), .width(6)) comparator_4 (
    .a(bitselector_1_out), .b(6'b011100), .eq(comparator_4_eq));  // open: gt, lt
  or or_1 (RegDst, comparator_4_eq, comparator_2_eq);
  Multiplexer #(.width(3)) multiplexer_1 (.in0(3'b010), .in1(3'b110), .out(multiplexer_1_out), .sel(Branch));
  or or_2 (RegWrite, ALUSrc, comparator_4_eq, comparator_2_eq);
  Multiplexer #(.width(3)) multiplexer_2 (
    .in0(multiplexer_1_out), .in1(3'b011), .out(ALUControl), .sel(comparator_4_eq));
endmodule
